# Fritzing sketch pratica (saved by Fritzing 1.0.1rc)

parts:
  M1 = ESP32-S3-DevKitC-1-N8R8-v1 [part_number=ESP32-S3-DevKitC-1-N8R8-v1]
  DHT1 = Humidity and Temperature Sensor DHT11
  R1 = Resistor [tolerance=±5% resistance=10k package="0603 [SMD]"]

nets:
  N1: M1.pin_1, M1.pin_2, DHT1.Vcc, R1.Pin_0
  N2: M1.pin_19, DHT1.Data-signal, R1.Pin_1
  N3: M1.pin_22, DHT1.GND_2

custom parts:
  ESP32-S3-DevKitC-1-N8R8-v1: ESP32-S3-DevKitC-1-N8R8-v1 This module is 44pins long (2x22) and 11 pins width.
  Humidity and Temperature Sensor DHT11: Digital relative humidity & temperature sensor DHT11
